# Fritzing sketch Keyboard (saved by Fritzing 0.9.3b)

parts:
  Esc = Cherry MX Keyswitch
  F1 = Cherry MX Keyswitch
  F2 = Cherry MX Keyswitch
  F3 = Cherry MX Keyswitch
  F4 = Cherry MX Keyswitch
  F5 = Cherry MX Keyswitch
  F6 = Cherry MX Keyswitch
  F7 = Cherry MX Keyswitch
  F8 = Cherry MX Keyswitch
  F9 = Cherry MX Keyswitch
  F10 = Cherry MX Keyswitch
  F12 = Cherry MX Keyswitch
  F11 = Cherry MX Keyswitch
  Scroll_Lock = Cherry MX Keyswitch
  Pause/Break = Cherry MX Keyswitch
  Print_Screen = Cherry MX Keyswitch
  Home = Cherry MX Keyswitch
  Page_Up = Cherry MX Keyswitch
  Insert = Cherry MX Keyswitch
  End = Cherry MX Keyswitch
  Page_Down = Cherry MX Keyswitch
  Delete = Cherry MX Keyswitch
  Down = Cherry MX Keyswitch
  Right = Cherry MX Keyswitch
  Left = Cherry MX Keyswitch
  Up = Cherry MX Keyswitch
  Num_Lock = Cherry MX Keyswitch
  / = Cherry MX Keyswitch
  * = Cherry MX Keyswitch
  - = Cherry MX Keyswitch
  + = Cherry MX Keyswitch
  9/Page_Up = Cherry MX Keyswitch
  7/Home = Cherry MX Keyswitch
  8/Up = Cherry MX Keyswitch
  6/Right = Cherry MX Keyswitch
  4/Left = Cherry MX Keyswitch
  5 = Cherry MX Keyswitch
  3/Page_Down = Cherry MX Keyswitch
  1/End = Cherry MX Keyswitch
  2/Down = Cherry MX Keyswitch
  Return = Cherry MX Keyswitch
  0/Insert = Cherry MX Keyswitch
  /Delete = Cherry MX Keyswitch
  Spacebar = Cherry MX Keyswitch
  RightCTRL = Cherry MX Keyswitch
  RightClick = Cherry MX Keyswitch
  FN = Cherry MX Keyswitch
  Right_Alt = Cherry MX Keyswitch
  Left_Alt = Cherry MX Keyswitch
  OS = Cherry MX Keyswitch
  LeftCTRL = Cherry MX Keyswitch
  Right_Shift = Cherry MX Keyswitch
  Enter = Cherry MX Keyswitch
  \/| = Cherry MX Keyswitch
  Backspace = Cherry MX Keyswitch
  //? = Cherry MX Keyswitch
  '/" = Cherry MX Keyswitch
  ]/} = Cherry MX Keyswitch
  =/+ = Cherry MX Keyswitch
  -/ = Cherry MX Keyswitch
  [/{ = Cherry MX Keyswitch
  ;/ = Cherry MX Keyswitch
  /> = Cherry MX Keyswitch
  /< = Cherry MX Keyswitch
  Left_Shift = Cherry MX Keyswitch
  CapsLock = Cherry MX Keyswitch
  Tab = Cherry MX Keyswitch
  `/~ = Cherry MX Keyswitch
  1/! = Cherry MX Keyswitch
  2/@ = Cherry MX Keyswitch
  3/# = Cherry MX Keyswitch
  4/$ = Cherry MX Keyswitch
  5/% = Cherry MX Keyswitch
  6/^ = Cherry MX Keyswitch
  7/& = Cherry MX Keyswitch
  8/* = Cherry MX Keyswitch
  9/( = Cherry MX Keyswitch
  0/) = Cherry MX Keyswitch
  Q = Cherry MX Keyswitch
  W = Cherry MX Keyswitch
  E = Cherry MX Keyswitch
  R = Cherry MX Keyswitch
  T = Cherry MX Keyswitch
  Y = Cherry MX Keyswitch
  U = Cherry MX Keyswitch
  I = Cherry MX Keyswitch
  O = Cherry MX Keyswitch
  P = Cherry MX Keyswitch
  A = Cherry MX Keyswitch
  S = Cherry MX Keyswitch
  D = Cherry MX Keyswitch
  F = Cherry MX Keyswitch
  G = Cherry MX Keyswitch
  H = Cherry MX Keyswitch
  J = Cherry MX Keyswitch
  K = Cherry MX Keyswitch
  L = Cherry MX Keyswitch
  Z = Cherry MX Keyswitch
  X = Cherry MX Keyswitch
  C = Cherry MX Keyswitch
  V = Cherry MX Keyswitch
  B = Cherry MX Keyswitch
  N = Cherry MX Keyswitch
  M = Cherry MX Keyswitch
  Esc_2 = Diode [package=diode-1n4148]
  F1_2 = Diode [package=diode-1n4148]
  F2_2 = Diode [package=diode-1n4148]
  F3_2 = Diode [package=diode-1n4148]
  F4_2 = Diode [package=diode-1n4148]
  F5_2 = Diode [package=diode-1n4148]
  F6_2 = Diode [package=diode-1n4148]
  F7_2 = Diode [package=diode-1n4148]
  F8_2 = Diode [package=diode-1n4148]
  F9_2 = Diode [package=diode-1n4148]
  F10_2 = Diode [package=diode-1n4148]
  F12_2 = Diode [package=diode-1n4148]
  F11_2 = Diode [package=diode-1n4148]
  Scroll_Lock_2 = Diode [package=diode-1n4148]
  Pause/Break_2 = Diode [package=diode-1n4148]
  Print_Screen_2 = Diode [package=diode-1n4148]
  Home_2 = Diode [package=diode-1n4148]
  Page_Up_2 = Diode [package=diode-1n4148]
  Insert_2 = Diode [package=diode-1n4148]
  End_2 = Diode [package=diode-1n4148]
  Page_Down_2 = Diode [package=diode-1n4148]
  Delete_2 = Diode [package=diode-1n4148]
  Down_2 = Diode [package=diode-1n4148]
  Right_2 = Diode [package=diode-1n4148]
  Left_2 = Diode [package=diode-1n4148]
  Up_2 = Diode [package=diode-1n4148]
  Num_Lock_2 = Diode [package=diode-1n4148]
  /_2 = Diode [package=diode-1n4148]
  *_2 = Diode [package=diode-1n4148]
  -_2 = Diode [package=diode-1n4148]
  +_2 = Diode [package=diode-1n4148]
  9/Page_Up_2 = Diode [package=diode-1n4148]
  7/Home_2 = Diode [package=diode-1n4148]
  8/Up_2 = Diode [package=diode-1n4148]
  6/Right_2 = Diode [package=diode-1n4148]
  4/Left_2 = Diode [package=diode-1n4148]
  5_2 = Diode [package=diode-1n4148]
  3/Page_Down_2 = Diode [package=diode-1n4148]
  1/End_2 = Diode [package=diode-1n4148]
  2/Down_2 = Diode [package=diode-1n4148]
  Return_2 = Diode [package=diode-1n4148]
  0/Insert_2 = Diode [package=diode-1n4148]
  /Delete_2 = Diode [package=diode-1n4148]
  Spacebar_2 = Diode [package=diode-1n4148]
  RightCTRL_2 = Diode [package=diode-1n4148]
  RightClick_2 = Diode [package=diode-1n4148]
  FN_2 = Diode [package=diode-1n4148]
  Right_Alt_2 = Diode [package=diode-1n4148]
  Left_Alt_2 = Diode [package=diode-1n4148]
  OS_2 = Diode [package=diode-1n4148]
  LeftCTRL_2 = Diode [package=diode-1n4148]
  Right_Shift_2 = Diode [package=diode-1n4148]
  Enter_2 = Diode [package=diode-1n4148]
  \/|_2 = Diode [package=diode-1n4148]
  Backspace_2 = Diode [package=diode-1n4148]
  //?_2 = Diode [package=diode-1n4148]  # not connected
  '/"_2 = Diode [package=diode-1n4148]
  ]/}_2 = Diode [package=diode-1n4148]
  =/+_2 = Diode [package=diode-1n4148]
  -/_2 = Diode [package=diode-1n4148]
  [/{_2 = Diode [package=diode-1n4148]
  ;/_2 = Diode [package=diode-1n4148]
  />_2 = Diode [package=diode-1n4148]
  /<_2 = Diode [package=diode-1n4148]
  Left_Shift_2 = Diode [package=diode-1n4148]
  CapsLock_2 = Diode [package=diode-1n4148]
  Tab_2 = Diode [package=diode-1n4148]
  `/~_2 = Diode [package=diode-1n4148]
  1/!_2 = Diode [package=diode-1n4148]
  2/@_2 = Diode [package=diode-1n4148]
  3/#_2 = Diode [package=diode-1n4148]
  4/$_2 = Diode [package=diode-1n4148]
  5/%_2 = Diode [package=diode-1n4148]
  6/^_2 = Diode [package=diode-1n4148]
  7/&_2 = Diode [package=diode-1n4148]
  8/*_2 = Diode [package=diode-1n4148]
  9/(_2 = Diode [package=diode-1n4148]
  0/)_2 = Diode [package=diode-1n4148]
  Q_2 = Diode [package=diode-1n4148]
  W_2 = Diode [package=diode-1n4148]
  E_2 = Diode [package=diode-1n4148]
  R_2 = Diode [package=diode-1n4148]
  T_2 = Diode [package=diode-1n4148]
  Y_2 = Diode [package=diode-1n4148]
  U_2 = Diode [package=diode-1n4148]
  I_2 = Diode [package=diode-1n4148]
  O_2 = Diode [package=diode-1n4148]
  P_2 = Diode [package=diode-1n4148]
  A_2 = Diode [package=diode-1n4148]
  S_2 = Diode [package=diode-1n4148]
  D_2 = Diode [package=diode-1n4148]
  F_2 = Diode [package=diode-1n4148]
  G_2 = Diode [package=diode-1n4148]
  H_2 = Diode [package=diode-1n4148]
  J_2 = Diode [package=diode-1n4148]
  K_2 = Diode [package=diode-1n4148]
  L_2 = Diode [package=diode-1n4148]
  Z_2 = Diode [package=diode-1n4148]
  X_2 = Diode [package=diode-1n4148]
  C_2 = Diode [package=diode-1n4148]
  V_2 = Diode [package=diode-1n4148]
  B_2 = Diode [package=diode-1n4148]
  N_2 = Diode [package=diode-1n4148]
  M_2 = Diode [package=diode-1n4148]

nets:
  N1: Esc.pin_4, Esc_2.A
  N2: F1.pin_4, F1_2.A
  N3: F2.pin_4, F2_2.A
  N4: F3.pin_4, F3_2.A
  N5: F4.pin_4, F4_2.A
  N6: F5.pin_4, F5_2.A
  N7: F6.pin_4, F6_2.A
  N8: F7.pin_4, F7_2.A
  N9: F8.pin_4, F8_2.A
  N10: F9.pin_4, F9_2.A
  N11: F10.pin_4, F10_2.A
  N12: F12.pin_4, F12_2.A
  N13: F11.pin_4, F11_2.A
  N14: Scroll_Lock.pin_4, Scroll_Lock_2.A
  N15: Pause/Break.pin_4, Pause/Break_2.A
  N16: Print_Screen.pin_4, Print_Screen_2.A
  N17: Home.pin_4, Home_2.A
  N18: Page_Up.pin_4, Page_Up_2.A
  N19: Insert.pin_4, Insert_2.A
  N20: End.pin_4, End_2.A
  N21: Page_Down.pin_4, Page_Down_2.A
  N22: Delete.pin_4, Delete_2.A
  N23: Down.pin_4, Down_2.A
  N24: Right.pin_4, Right_2.A
  N25: Left.pin_4, Left_2.A
  N26: Up.pin_4, Up_2.A
  N27: Num_Lock.pin_4, Num_Lock_2.A
  N28: /.pin_4, /_2.A
  N29: *.pin_4, *_2.A
  N30: -.pin_4, -_2.A
  N31: +.pin_4, +_2.A
  N32: 9/Page_Up.pin_4, 9/Page_Up_2.A
  N33: 7/Home.pin_4, 7/Home_2.A
  N34: 8/Up.pin_4, 8/Up_2.A
  N35: 6/Right.pin_4, 6/Right_2.A
  N36: 4/Left.pin_4, 4/Left_2.A
  N37: 5.pin_4, 5_2.A
  N38: 3/Page_Down.pin_4, 3/Page_Down_2.A
  N39: 1/End.pin_4, 1/End_2.A
  N40: 2/Down.pin_4, 2/Down_2.A
  N41: Return.pin_4, Return_2.A
  N42: 0/Insert.pin_4, 0/Insert_2.A
  N43: /Delete.pin_4, /Delete_2.A
  N44: Spacebar.pin_4, Spacebar_2.A
  N45: RightCTRL.pin_4, RightCTRL_2.A
  N46: RightClick.pin_4, RightClick_2.A
  N47: FN.pin_4, FN_2.A
  N48: Right_Alt.pin_4, Right_Alt_2.A
  N49: Left_Alt.pin_4, Left_Alt_2.A
  N50: OS.pin_4, OS_2.A
  N51: LeftCTRL.pin_4, LeftCTRL_2.A
  N52: Right_Shift.pin_4, Right_Shift_2.A
  N53: Enter.pin_4, Enter_2.A
  N54: \/|.pin_4, \/|_2.A
  N55: Backspace.pin_4, Backspace_2.A
  N56: //?.pin_4, //?.pin_6, //?.pin_8
  N57: '/".pin_4, '/"_2.A
  N58: ]/}.pin_4, ]/}_2.A
  N59: =/+.pin_4, =/+_2.A
  N60: -/.pin_4, -/_2.A
  N61: [/{.pin_4, [/{_2.A
  N62: ;/.pin_4, ;/_2.A
  N63: />.pin_4, />_2.A
  N64: /<.pin_4, /<_2.A
  N65: Left_Shift.pin_4, Left_Shift_2.A
  N66: CapsLock.pin_4, CapsLock_2.A
  N67: Tab.pin_4, Tab_2.A
  N68: `/~.pin_4, `/~_2.A
  N69: 1/!.pin_4, 1/!_2.A
  N70: 2/@.pin_4, 2/@_2.A
  N71: 3/#.pin_4, 3/#_2.A
  N72: 4/$.pin_4, 4/$_2.A
  N73: 5/%.pin_4, 5/%_2.A
  N74: 6/^.pin_4, 6/^_2.A
  N75: 7/&.pin_4, 7/&_2.A
  N76: 8/*.pin_4, 8/*_2.A
  N77: 9/(.pin_4, 9/(_2.A
  N78: 0/).pin_4, 0/)_2.A
  N79: Q.pin_4, Q_2.A
  N80: W.pin_4, W_2.A
  N81: E.pin_4, E_2.A
  N82: R.pin_4, R_2.A
  N83: T.pin_4, T_2.A
  N84: Y.pin_4, Y_2.A
  N85: U.pin_4, U_2.A
  N86: I.pin_4, I_2.A
  N87: O.pin_4, O_2.A
  N88: P.pin_4, P_2.A
  N89: A.pin_4, A_2.A
  N90: S.pin_4, S_2.A
  N91: D.pin_4, D_2.A
  N92: F.pin_4, F_2.A
  N93: G.pin_4, G_2.A
  N94: H.pin_4, H_2.A
  N95: J.pin_4, J_2.A
  N96: K.pin_4, K_2.A
  N97: L.pin_4, L_2.A
  N98: Z.pin_4, Z_2.A
  N99: X.pin_4, X_2.A
  N100: C.pin_4, C_2.A
  N101: V.pin_4, V_2.A
  N102: B.pin_4, B_2.A
  N103: N.pin_4, N_2.A
  N104: M.pin_4, M_2.A
